// Logisim project lab1.circ as structural Verilog: 4 circuits, main circuit ALU
module ALU (
  input  [31:0] S1,
  input  [31:0] S2,
  input  [3:0] ALU_Function,
  output [31:0] Result,
  output N,
  output Z,
  output C,
  output V
);

  wire CMN_Carry, CMP_Carry, decoder_1_out2, decoder_1_out3, decoder_1_out4, decoder_1_out7,
       multiplexer_2_out, Shift_Carry;
  wire [31:0] ANDS, BICS, CMN, CMP, EORS, MVNS, not_1_out, ORRS, Shift;

  assign not_1_out = ~S2;  // NOT_Gate not_1, 32 bits wide
  assign MVNS = ~S2;  // NOT_Gate not_2, 32 bits wide
  Decoder #(.select(4), .enable("false")) decoder_1 (
    .out2(decoder_1_out2), .out3(decoder_1_out3), .out4(decoder_1_out4), .out7(decoder_1_out7),
    .sel(ALU_Function));  // open: out0, out1, out5, out6, out8, out9, out10, out11, out12, out13, out14, out15
  assign ANDS = S1 & S2;  // AND_Gate and_1, 32 bits wide
  assign EORS = S1 ^ S2;  // XOR_Gate xor_1, 32 bits wide
  assign ORRS = S1 | S2;  // OR_Gate or_1, 32 bits wide
  assign BICS = S1 & not_1_out;  // AND_Gate and_2, 32 bits wide
  Full_Adder_Subtractor full_adder_subtractor_1 (.Rd(S1), .Rn(S2), .Sub_Bit(1'b1), .Result(CMP), .Cout(CMP_Carry));
  Full_Adder_Subtractor full_adder_subtractor_2 (.Rd(S1), .Rn(S2), .Sub_Bit(1'b0), .Result(CMN), .Cout(CMN_Carry));
  // Shift_Unit shift_unit_1: pin names not known; wires that end beside it: S1, S2[7:0], decoder_1_out2, decoder_1_out3, decoder_1_out4, decoder_1_out7, Shift, Shift_Carry
  Multiplexer #(.select(4), .width(32), .enable("false")) multiplexer_1 (
    .in0(ANDS), .in1(EORS), .in2(Shift), .in3(Shift), .in4(Shift), .in7(Shift), .in8(ANDS), .in10(CMP),
    .in11(CMN), .in12(ORRS), .in14(BICS), .in15(MVNS), .out(Result), .sel(ALU_Function));  // open: in5, in6, in9, in13
  Zero_Negative_Test zero_negative_test_1 (.Result(Result), .Zero(Z), .Negative(N));
  Multiplexer #(.select(4), .enable("false")) multiplexer_2 (
    .in10(1'b1), .in11(1'b0), .out(multiplexer_2_out), .sel(ALU_Function));  // open: in0, in1, in2, in3, in4, in5, in6, in7, in8, in9, in12, in13, in14, in15
  Multiplexer #(.select(4), .enable("false")) multiplexer_3 (
    .in2(Shift_Carry), .in3(Shift_Carry), .in4(Shift_Carry), .in7(Shift_Carry), .in10(CMP_Carry),
    .in11(CMN_Carry), .out(C), .sel(ALU_Function));  // open: in0, in1, in5, in6, in8, in9, in12, in13, in14, in15
  Overflow_Test overflow_test_1 (.Rd(S1), .Rn(S2), .Result(Result), .Sub_Bit(multiplexer_2_out), .Overflow(V));

  // Other names for the same wires on the sheet: Carry = C; Input1[31:0] = S1; Input2[31:0] = S2; Negative = N;
  //   Overflow = V; TST[31:0] = ANDS; Zero = Z

  // Notes on the sheet:
  //   Tim Whitaker
  //   Jay DiFuria
endmodule

module Zero_Negative_Test (
  input  [31:0] Result,
  output Zero,
  output Negative
);

  nor nor_1 (Zero, Result[0], Result[1], Result[2], Result[3], Result[4], Result[5], Result[6], Result[7], Result[8], Result[9], Result[10], Result[11], Result[12], Result[13], Result[14], Result[15], Result[16], Result[17], Result[18], Result[19], Result[20], Result[21], Result[22], Result[23], Result[24], Result[25], Result[26], Result[27], Result[28], Result[29], Result[30], Result[31]);

  assign Negative = Result[31];
endmodule

module Full_Adder_Subtractor (
  input  [31:0] Rd,
  input  [31:0] Rn,
  input  Sub_Bit,
  output [31:0] Result,
  output Cout
);

  wire [31:0] bit_extender_1_out, xor_1_out;

  assign bit_extender_1_out = {{31{Sub_Bit}}, Sub_Bit};  // Bit_Extender bit_extender_1
  Adder #(.width(32)) adder_1 (.a(Rd), .b(xor_1_out), .out(Result), .cin(Sub_Bit), .cout(Cout));
  assign xor_1_out = Rn ^ bit_extender_1_out;  // XOR_Gate xor_1, 32 bits wide
endmodule

module Overflow_Test (
  input  [31:0] Rd,
  input  [31:0] Rn,
  input  [31:0] Result,
  input  Sub_Bit,
  output Overflow
);

  wire Add_Overflow, and_1_out, and_2_out, and_3_out, and_4_out, not_1_out, not_2_out, not_3_out, not_4_out,
       not_5_out, not_6_out, Sub_Overflow;

  and and_1 (and_1_out, Rd[31], Rn[31], not_1_out);
  not not_1 (not_1_out, Result[31]);
  not not_2 (not_2_out, Rd[31]);
  not not_3 (not_3_out, Rn[31]);
  and and_2 (and_2_out, not_2_out, not_3_out, Result[31]);
  not not_4 (not_4_out, Rn[31]);
  and and_3 (and_3_out, Rd[31], not_4_out, not_5_out);
  not not_5 (not_5_out, Result[31]);
  not not_6 (not_6_out, Rd[31]);
  and and_4 (and_4_out, not_6_out, Rn[31], Result[31]);
  or or_1 (Add_Overflow, and_1_out, and_2_out);
  or or_2 (Sub_Overflow, and_3_out, and_4_out);
  Multiplexer #(.enable("false")) multiplexer_1 (.in0(Add_Overflow), .in1(Sub_Overflow), .out(Overflow), .sel(Sub_Bit));
endmodule
