// Logisim project lab2.circ as structural Verilog: 4 circuits, main circuit SingleCycleARM
module SingleCycleARM (
  input  CLK,
  output [31:0] PC,
  output [15:0] Instruction,
  output Write_Desination,
  output [2:0] D_address,
  output [31:0] D_data,
  output N,
  output Z,
  output C,
  output V,
  output Memory_write,
  output [6:0] M_address,
  output [31:0] M_data_in
);

  wire alu_1_p3, alu_1_p4, alu_1_p6, alu_1_p7, B, CondB, CV_Write, MEM_Mux, not_1_out, NZ_Write,
       register_file_1_p7;
  wire [1:0] ALU_Mux, RF_Mux;
  wire [2:0] multiplexer_1_out, Rm_imm3, Rn;
  wire [3:0] ALU_Op, Cond;
  wire [4:0] imm5, shifter_1_out;
  wire [7:0] imm8;
  wire [9:0] Op_Code;
  wire [10:0] imm11;
  wire [31:0] bit_extender_1_out, bit_extender_2_out, multiplexer_2_out, NextPC, ram_2_data;
  wire [31:7] alu_1_p8;

  Register #(.width(32)) register_1 (.D(NextPC), .en(1'b1), .Q(PC), .clk(CLK));  // open: clr
  Multiplexer #(.select(2), .width(3), .enable("false")) multiplexer_1 (
    .in0(Rn), .in1(Rm_imm3), .in2(D_address), .in3(Rm_imm3), .out(multiplexer_1_out), .sel(RF_Mux));
  assign bit_extender_1_out = {{29{1'b0}}, Rm_imm3};  // Bit_Extender bit_extender_1
  RAM #(.addrWidth(7), .dataWidth(16)) ram_1 (.addr(PC[7:1]), .data(Instruction));  // open: sel, clk, ld, clr
  Shifter #(.width(5)) shifter_1 (.in(imm5), .\dist (3'b010), .out(shifter_1_out));
  // Register_File register_file_1: pin names not known; wires that end beside it: Rn, multiplexer_1_out, D_address, D_data, Write_Desination, CLK, register_file_1_p7, M_data_in
  assign bit_extender_2_out = {{27{1'b0}}, shifter_1_out};  // Bit_Extender bit_extender_2
  Multiplexer #(.select(2), .width(32), .enable("false")) multiplexer_2 (
    .in0(M_data_in), .in1(bit_extender_2_out), .in2(bit_extender_1_out), .out(multiplexer_2_out),
    .sel(ALU_Mux));  // open: in3
  // ALU alu_1: pin names not known; wires that end beside it: register_file_1_p7, multiplexer_2_out, alu_1_p3, alu_1_p4, ALU_Op, alu_1_p6, alu_1_p7, {alu_1_p8, M_address}
  Control control_1 (
    .Op(Op_Code), .B(B), .CondB(CondB), .ALU_Op(ALU_Op), .RF_Mux(RF_Mux), .ALU_Mux(ALU_Mux),
    .Mem_Mux(MEM_Mux), .MemWrite(Memory_write), .DestinationWrite(Write_Desination), .NZ_Write(NZ_Write),
    .CV_Write(CV_Write));
  D_Flip_Flop d_ff_1 (.clk(CLK), .D(alu_1_p7), .Q(V), .en(CV_Write));  // open: Qn, preset, reset
  D_Flip_Flop d_ff_2 (.clk(CLK), .D(alu_1_p6), .Q(C), .en(CV_Write));  // open: Qn, preset, reset
  D_Flip_Flop d_ff_3 (.clk(CLK), .D(alu_1_p4), .Q(Z), .en(NZ_Write));  // open: Qn, preset, reset
  D_Flip_Flop d_ff_4 (.clk(CLK), .D(alu_1_p3), .Q(N), .en(NZ_Write));  // open: Qn, preset, reset
  not not_1 (not_1_out, Memory_write);
  RAM #(.addrWidth(7), .dataWidth(32), .bus("separate")) ram_2 (
    .addr(M_address), .din(M_data_in), .data(ram_2_data), .str(Memory_write), .clk(CLK), .ld(not_1_out));  // open: sel, clr
  NextPC nextpc_1 (
    .PCplus2(PC), .imm11(imm11), .B(B), .Bcond(CondB), .N(N), .Z(Z), .C(C), .V(V), .Cond(Cond),
    .NextPC(NextPC));
  Multiplexer #(.width(32), .enable("false")) multiplexer_3 (
    .in0({alu_1_p8, M_address}), .in1(ram_2_data), .out(D_data), .sel(MEM_Mux));
  Instruction_Decode instruction_decode_1 (
    .Instruction(Instruction), .Op_code(Op_Code), .Rd(D_address), .Rn(Rn), .Rm_imm3(Rm_imm3), .imm5(imm5),
    .imm8(imm8), .imm11(imm11), .Cond(Cond));

  // Other names for the same wires on the sheet: Destination_Write = Write_Desination; MEM_Write = Memory_write;
  //   Rd[2:0] = D_address

  // Notes on the sheet:
  //   Tim Whitker
  //   Jay DiFuria
endmodule

module Control (
  input  [9:0] Op,
  output B,
  output CondB,
  output [3:0] ALU_Op,
  output [1:0] RF_Mux,
  output [1:0] ALU_Mux,
  output Mem_Mux,
  output MemWrite,
  output DestinationWrite,
  output NZ_Write,
  output CV_Write
);

  wire and_1_out, and_4_out, comparator_1_eq, decoder_1_out4, decoder_1_out11;
  wire [3:0] multiplexer_1_out, multiplexer_2_out;

  Decoder #(.select(4), .enable("false")) decoder_1 (
    .out1(CV_Write), .out4(decoder_1_out4), .out6(ALU_Mux[0]), .out11(decoder_1_out11), .out13(CondB),
    .out14(B), .sel(Op[9:6]));  // open: out0, out2, out3, out5, out7, out8, out9, out10, out12, out15
  Multiplexer #(.width(4), .enable("false")) multiplexer_1 (
    .in0(4'b1011), .in1(4'b1010), .out(multiplexer_1_out), .sel(Op[3]));
  Comparator #(.width(4)) comparator_1 (.a(Op[3:0]), .b(4'b1111), .eq(comparator_1_eq));  // open: gt, lt
  Multiplexer #(.width(4), .enable("false")) multiplexer_2 (
    .in0(multiplexer_1_out), .in1(4'b1011), .out(multiplexer_2_out), .sel(ALU_Mux[0]));
  Multiplexer #(.width(4), .enable("false")) multiplexer_3 (
    .in0(multiplexer_2_out), .in1(Op[3:0]), .out(ALU_Op), .sel(decoder_1_out4));
  and and_1 (and_1_out, comparator_1_eq, decoder_1_out4);
  and and_2 (ALU_Mux[1], CV_Write, Op[4]);
  and and_3 (MemWrite, ALU_Mux[0], ~Op[5]);  // AND_Gate
  and and_4 (and_4_out, Op[5], ALU_Mux[0]);
  or or_1 (DestinationWrite, and_4_out, decoder_1_out4, CV_Write);
  or or_2 (NZ_Write, CV_Write, decoder_1_out4);
  or or_3 (RF_Mux[0], and_1_out, CV_Write);
  or or_4 (RF_Mux[1], ALU_Mux[0], decoder_1_out4);

  assign Mem_Mux = ALU_Mux[0];

  // Notes on the sheet:
  //   B
  //   B{cond}
  //   NOP
  //   REGS
  //   LDR/STR
  //   ADDS/SUBS
endmodule

module NextPC (
  input  [31:0] PCplus2,
  input  [10:0] imm11,
  input  B,
  input  Bcond,
  input  N,
  input  Z,
  input  C,
  input  V,
  input  [3:0] Cond,
  output [31:0] NextPC
);

  wire and_1_out, multiplexer_3_out, not_1_out, not_2_out, not_3_out, not_4_out;
  wire [31:0] adder_1_out, adder_2_out, adder_3_out, adder_4_out, adder_5_out, bit_extender_1_out,
       bit_extender_2_out, multiplexer_1_out;

  Adder #(.width(32)) adder_1 (.a(32'h2), .b(PCplus2), .out(adder_1_out));  // open: cin, cout
  assign bit_extender_1_out = {{20{imm11[10]}}, {imm11, 1'b0}};  // Bit_Extender bit_extender_1
  Adder #(.width(32)) adder_2 (.a(adder_1_out), .b(bit_extender_1_out), .out(adder_2_out), .cin(1'b0));  // open: cout
  Adder #(.width(32)) adder_3 (.a(32'h2), .b(adder_2_out), .out(adder_3_out));  // open: cin, cout
  assign bit_extender_2_out = {{23{imm11[7]}}, {imm11[7:0], 1'b0}};  // Bit_Extender bit_extender_2
  Adder #(.width(32)) adder_4 (.a(32'h2), .b(adder_5_out), .out(adder_4_out));  // open: cin, cout
  Adder #(.width(32)) adder_5 (.a(adder_1_out), .b(bit_extender_2_out), .out(adder_5_out), .cin(1'b0));  // open: cout
  not not_1 (not_1_out, Z);
  not not_2 (not_2_out, C);
  not not_3 (not_3_out, N);
  not not_4 (not_4_out, V);
  Multiplexer #(.width(32), .enable("false")) multiplexer_1 (
    .in0(adder_1_out), .in1(adder_3_out), .out(multiplexer_1_out), .sel(B));
  Multiplexer #(.width(32), .enable("false")) multiplexer_2 (
    .in0(multiplexer_1_out), .in1(adder_4_out), .out(NextPC), .sel(and_1_out));
  and and_1 (and_1_out, Bcond, multiplexer_3_out);
  Multiplexer #(.select(4), .enable("false")) multiplexer_3 (
    .in0(Z), .in1(not_1_out), .in2(C), .in3(not_2_out), .in4(N), .in5(not_3_out), .in6(V), .in7(not_4_out),
    .in8(1'b0), .in9(1'b0), .in10(1'b0), .in11(1'b0), .in12(1'b0), .in13(1'b0), .in14(1'b0), .in15(1'b0),
    .out(multiplexer_3_out), .sel(Cond));
endmodule

module Instruction_Decode (
  input  [15:0] Instruction,
  output [9:0] Op_code,
  output [2:0] Rd,
  output [2:0] Rn,
  output [2:0] Rm_imm3,
  output [4:0] imm5,
  output [7:0] imm8,
  output [10:0] imm11,
  output [3:0] Cond
);


  assign Cond = Instruction[11:8];
  assign imm5 = Instruction[10:6];
  assign imm8 = Instruction[7:0];
  assign imm11 = Instruction[10:0];
  assign Op_code = Instruction[15:6];
  assign Rd = Instruction[2:0];
  assign Rm_imm3 = Instruction[8:6];
  assign Rn = Instruction[5:3];
endmodule
