// Logisim project lab3.circ as structural Verilog: 7 circuits, main circuit PipelinedARM
module PipelinedARM (
  input  CLK,
  output [31:0] IF_PC,
  output [15:0] IF_Instruction,
  output EX_N,
  output EX_Z,
  output EX_C,
  output EX_V,
  output WB_Write_Desination,
  output [2:0] WB_D_address,
  output [31:0] WB_D_data,
  output WB_Memory_write,
  output [6:0] WB_M_address,
  output [31:0] WB_M_data_in
);

  Pipeline_Implementation pipeline_implementation_1 (
    .CLK(CLK), .IF_PC(IF_PC), .IF_Instruction(IF_Instruction), .EX_N(EX_N), .EX_Z(EX_Z), .EX_C(EX_C),
    .EX_V(EX_V), .WB_Write_Desination(WB_Write_Desination), .WB_D_address(WB_D_address),
    .WB_D_data(WB_D_data), .WB_Memory_write(WB_Memory_write), .WB_M_address(WB_M_address),
    .WB_M_data_in(WB_M_data_in));
endmodule

module control (
  input  [9:0] Op,
  output B,
  output CondB,
  output [3:0] ALU_Op,
  output [1:0] RF_Mux,
  output [1:0] ALU_Mux,
  output Mem_Mux,
  output MemWrite,
  output DestinationWrite,
  output NZ_Write,
  output CV_Write
);

  wire and_1_out, and_4_out, comparator_1_eq, decoder_1_out4, decoder_1_out11;
  wire [3:0] multiplexer_1_out, multiplexer_2_out;

  Decoder #(.select(4), .enable("false")) decoder_1 (
    .out1(CV_Write), .out4(decoder_1_out4), .out6(ALU_Mux[0]), .out11(decoder_1_out11), .out13(CondB),
    .out14(B), .sel(Op[9:6]));  // open: out0, out2, out3, out5, out7, out8, out9, out10, out12, out15
  Multiplexer #(.width(4), .enable("false")) multiplexer_1 (
    .in0(4'b1011), .in1(4'b1010), .out(multiplexer_1_out), .sel(Op[3]));
  Comparator #(.width(4)) comparator_1 (.a(Op[3:0]), .b(4'b1111), .eq(comparator_1_eq));  // open: gt, lt
  Multiplexer #(.width(4), .enable("false")) multiplexer_2 (
    .in0(multiplexer_1_out), .in1(4'b1011), .out(multiplexer_2_out), .sel(ALU_Mux[0]));
  Multiplexer #(.width(4), .enable("false")) multiplexer_3 (
    .in0(multiplexer_2_out), .in1(Op[3:0]), .out(ALU_Op), .sel(decoder_1_out4));
  and and_1 (and_1_out, comparator_1_eq, decoder_1_out4);
  and and_2 (ALU_Mux[1], CV_Write, Op[4]);
  and and_3 (MemWrite, ALU_Mux[0], ~Op[5]);  // AND_Gate
  and and_4 (and_4_out, Op[5], ALU_Mux[0]);
  or or_1 (DestinationWrite, and_4_out, decoder_1_out4, CV_Write);
  or or_2 (NZ_Write, CV_Write, decoder_1_out4);
  or or_3 (RF_Mux[0], and_1_out, CV_Write);
  or or_4 (RF_Mux[1], ALU_Mux[0], decoder_1_out4);

  assign Mem_Mux = ALU_Mux[0];

  // Notes on the sheet:
  //   B
  //   B{cond}
  //   NOP
  //   REGS
  //   LDR/STR
  //   ADDS/SUBS
endmodule

module Pipeline_Implementation (
  input  CLK,
  output [31:0] IF_PC,
  output [15:0] IF_Instruction,
  output EX_N,
  output EX_Z,
  output EX_C,
  output EX_V,
  output WB_Write_Desination,
  output [2:0] WB_D_address,
  output [31:0] WB_D_data,
  output WB_Memory_write,
  output [6:0] WB_M_address,
  output [31:0] WB_M_data_in
);

  wire alu_1_p3, alu_1_p4, alu_1_p6, alu_1_p7, control_1_b, control_1_condb, control_1_cv_write,
       control_1_destinationwrite, control_1_mem_mux, control_1_memwrite, control_1_nz_write,
       load_use_hazard_1_s1_mux, load_use_hazard_1_s2_mux, not_1_out, sr_2_1_cv_write_2,
       sr_2_1_destinationwrite_2, sr_2_1_mem_mux_2, sr_2_1_memwrite_2, sr_2_1_nz_write_2, sr_3_1_mem_mux_2;
  wire [1:0] control_1_alu_mux, control_1_rf_mux;
  wire [2:0] multiplexer_1_out, sr_1_1_result_2, sr_2_1_rd_2, sr_2_1_rm_2, sr_2_1_rn_2;
  wire [3:0] control_1_alu_op, sr_2_1_alu_op_2;
  wire [4:0] shifter_1_out;
  wire [15:0] sr_1_1_result;
  wire [31:0] adder_1_out, alu_1_p8, bit_extender_1_out, bit_extender_2_out, multiplexer_2_out,
       multiplexer_3_out, multiplexer_4_out, ram_2_data, register_file_1_p7, register_file_1_p8,
       sr_2_1_m_data_2, sr_2_1_s1_2, sr_2_1_s2_2, sr_3_1_alu_data_2;

  Adder #(.width(32)) adder_1 (.a(IF_PC), .b(32'h2), .out(adder_1_out));  // open: cin, cout
  Register #(.width(32)) register_1 (.D(adder_1_out), .en(1'b1), .Q(IF_PC), .clk(CLK));  // open: clr
  RAM #(.addrWidth(7), .dataWidth(16)) ram_1 (.addr(IF_PC[7:1]), .data(IF_Instruction));  // open: sel, clk, ld, clr
  SR_1 sr_1_1 (
    .clk(CLK), .Instruction(IF_Instruction),
    .Result({sr_1_1_result[15:6], sr_1_1_result_2, sr_1_1_result[2:0]}));
  control control_1 (
    .Op(sr_1_1_result[15:6]), .B(control_1_b), .CondB(control_1_condb), .ALU_Op(control_1_alu_op),
    .RF_Mux(control_1_rf_mux), .ALU_Mux(control_1_alu_mux), .Mem_Mux(control_1_mem_mux),
    .MemWrite(control_1_memwrite), .DestinationWrite(control_1_destinationwrite),
    .NZ_Write(control_1_nz_write), .CV_Write(control_1_cv_write));
  Multiplexer #(.select(2), .width(3), .enable("false")) multiplexer_1 (
    .in0(sr_1_1_result_2), .in1(sr_1_1_result[8:6]), .in2(sr_1_1_result[2:0]), .in3(sr_1_1_result[8:6]),
    .out(multiplexer_1_out), .sel(control_1_rf_mux));
  Shifter #(.width(5)) shifter_1 (.in(sr_1_1_result[10:6]), .\dist (3'b010), .out(shifter_1_out));
  assign bit_extender_1_out = {{29{1'b0}}, sr_1_1_result[8:6]};  // Bit_Extender bit_extender_1
  assign bit_extender_2_out = {{27{1'b0}}, shifter_1_out};  // Bit_Extender bit_extender_2
  // Register_File register_file_1: pin names not known; wires that end beside it: sr_1_1_result_2, multiplexer_1_out, WB_D_address, WB_D_data, WB_Write_Desination, CLK, register_file_1_p7, register_file_1_p8
  Multiplexer #(.select(2), .width(32), .enable("false")) multiplexer_2 (
    .in0(register_file_1_p8), .in1(bit_extender_2_out), .in2(bit_extender_1_out), .out(multiplexer_2_out),
    .sel(control_1_alu_mux));  // open: in3
  SR_2 sr_2_1 (
    .clk(CLK), .S1(register_file_1_p7), .S2(multiplexer_2_out), .B(control_1_b), .CondB(control_1_condb),
    .ALU_Op(control_1_alu_op), .RF_Mux(control_1_rf_mux), .ALU_Mux(control_1_alu_mux),
    .Mem_Mux(control_1_mem_mux), .MemWrite(control_1_memwrite),
    .DestinationWrite(control_1_destinationwrite), .NZ_Write(control_1_nz_write),
    .CV_Write(control_1_cv_write), .Rd(sr_1_1_result[2:0]), .m_data(register_file_1_p8),
    .Rm(sr_1_1_result[8:6]), .Rn(sr_1_1_result_2), .S1_2(sr_2_1_s1_2), .S2_2(sr_2_1_s2_2),
    .ALU_Op_2(sr_2_1_alu_op_2), .Mem_Mux_2(sr_2_1_mem_mux_2), .MemWrite_2(sr_2_1_memwrite_2),
    .DestinationWrite_2(sr_2_1_destinationwrite_2), .NZ_Write_2(sr_2_1_nz_write_2),
    .CV_Write_2(sr_2_1_cv_write_2), .Rd_2(sr_2_1_rd_2), .m_data_2(sr_2_1_m_data_2), .Rm_2(sr_2_1_rm_2),
    .Rn_2(sr_2_1_rn_2));  // open: B_2, CondB_2, RF_Mux_2, ALU_Mux_2
  load_use_hazard load_use_hazard_1 (
    .WB_write_dest(WB_Write_Desination), .wb_rd(WB_D_address), .ex_rm(sr_2_1_rm_2), .ex_rn(sr_2_1_rn_2),
    .S1_mux(load_use_hazard_1_s1_mux), .S2_mux(load_use_hazard_1_s2_mux));
  Multiplexer #(.width(32), .enable("false")) multiplexer_3 (
    .in0(sr_2_1_s1_2), .in1({sr_3_1_alu_data_2[31:9], WB_M_address, sr_3_1_alu_data_2[1:0]}),
    .out(multiplexer_3_out), .sel(load_use_hazard_1_s1_mux));
  Multiplexer #(.width(32), .enable("false")) multiplexer_4 (
    .in0(sr_2_1_s2_2), .in1(WB_M_data_in), .out(multiplexer_4_out), .sel(load_use_hazard_1_s2_mux));
  // ALU alu_1: pin names not known; wires that end beside it: multiplexer_3_out, multiplexer_4_out, alu_1_p3, alu_1_p4, sr_2_1_alu_op_2, alu_1_p6, alu_1_p7, alu_1_p8
  D_Flip_Flop d_ff_1 (.clk(CLK), .D(alu_1_p7), .Q(EX_V), .en(sr_2_1_cv_write_2));  // open: Qn, preset, reset
  D_Flip_Flop d_ff_2 (.clk(CLK), .D(alu_1_p6), .Q(EX_C), .en(sr_2_1_cv_write_2));  // open: Qn, preset, reset
  D_Flip_Flop d_ff_3 (.clk(CLK), .D(alu_1_p4), .Q(EX_Z), .en(sr_2_1_nz_write_2));  // open: Qn, preset, reset
  D_Flip_Flop d_ff_4 (.clk(CLK), .D(alu_1_p3), .Q(EX_N), .en(sr_2_1_nz_write_2));  // open: Qn, preset, reset
  SR_3 sr_3_1 (
    .clk(CLK), .alu_data(alu_1_p8), .m_data(sr_2_1_m_data_2), .V(EX_V), .C(EX_C), .Z(EX_Z), .N(EX_N),
    .mem_write(sr_2_1_memwrite_2), .mem_mux(sr_2_1_mem_mux_2), .Rd(sr_2_1_rd_2),
    .WB_write(sr_2_1_destinationwrite_2),
    .alu_data_2({sr_3_1_alu_data_2[31:9], WB_M_address, sr_3_1_alu_data_2[1:0]}), .m_data_2(WB_M_data_in),
    .mem_write_2(WB_Memory_write), .mem_mux_2(sr_3_1_mem_mux_2), .Rd_2(WB_D_address),
    .WB_write_2(WB_Write_Desination));  // open: V_2, C_2, Z_2, N_2
  not not_1 (not_1_out, WB_Memory_write);
  RAM #(.addrWidth(7), .dataWidth(32), .bus("separate")) ram_2 (
    .addr(WB_M_address), .din(WB_M_data_in), .data(ram_2_data), .str(WB_Memory_write), .clk(CLK),
    .ld(not_1_out));  // open: sel, clr
  Multiplexer #(.width(32), .enable("false")) multiplexer_5 (
    .in0({sr_3_1_alu_data_2[31:9], WB_M_address, sr_3_1_alu_data_2[1:0]}), .in1(ram_2_data), .out(WB_D_data),
    .sel(sr_3_1_mem_mux_2));

  // Other names for the same wires on the sheet: WB_m_addr[6:0] = WB_M_address; WB_d_addr[2:0] = WB_D_address;
  //   WB_dest = WB_Write_Desination; WB_m_data[31:0] = WB_M_data_in; WB_mem_write = WB_Memory_write

  // Notes on the sheet:
  //   Jay DiFuria
  //   Tim Whitaker
endmodule

// SR1
module SR_1 (
  input  clk,
  input  [15:0] Instruction,
  output [15:0] Result
);

  Register #(.width(16)) register_1 (.D(Instruction), .en(1'b1), .Q(Result), .clk(clk));  // open: clr
endmodule

// SR2
module SR_2 (
  input  clk,
  input  [31:0] S1,
  input  [31:0] S2,
  input  B,
  input  CondB,
  input  [3:0] ALU_Op,
  input  [1:0] RF_Mux,
  input  [1:0] ALU_Mux,
  input  Mem_Mux,
  input  MemWrite,
  input  DestinationWrite,
  input  NZ_Write,
  input  CV_Write,
  input  [2:0] Rd,
  input  [31:0] m_data,
  input  [2:0] Rm,
  input  [2:0] Rn,
  output [31:0] S1_2,
  output [31:0] S2_2,
  output B_2,
  output CondB_2,
  output [3:0] ALU_Op_2,
  output [1:0] RF_Mux_2,
  output [1:0] ALU_Mux_2,
  output Mem_Mux_2,
  output MemWrite_2,
  output DestinationWrite_2,
  output NZ_Write_2,
  output CV_Write_2,
  output [2:0] Rd_2,
  output [31:0] m_data_2,
  output [2:0] Rm_2,
  output [2:0] Rn_2
);

  Register #(.width(32)) register_1 (.D(S1), .en(1'b1), .Q(S1_2), .clk(clk));  // open: clr
  Register #(.width(32)) register_2 (.D(S2), .en(1'b1), .Q(S2_2), .clk(clk));  // open: clr
  Register #(.width(1)) register_3 (.D(B), .en(1'b1), .Q(B_2), .clk(clk));  // open: clr
  Register #(.width(1)) register_4 (.D(CondB), .en(1'b1), .Q(CondB_2), .clk(clk));  // open: clr
  Register #(.width(4)) register_5 (.D(ALU_Op), .en(1'b1), .Q(ALU_Op_2), .clk(clk));  // open: clr
  Register #(.width(2)) register_6 (.D(RF_Mux), .en(1'b1), .Q(RF_Mux_2), .clk(clk));  // open: clr
  Register #(.width(2)) register_7 (.D(ALU_Mux), .en(1'b1), .Q(ALU_Mux_2), .clk(clk));  // open: clr
  Register #(.width(1)) register_8 (.D(Mem_Mux), .en(1'b1), .Q(Mem_Mux_2), .clk(clk));  // open: clr
  Register #(.width(1)) register_9 (.D(MemWrite), .en(1'b1), .Q(MemWrite_2), .clk(clk));  // open: clr
  Register #(.width(1)) register_10 (.D(DestinationWrite), .en(1'b1), .Q(DestinationWrite_2), .clk(clk));  // open: clr
  Register #(.width(1)) register_11 (.D(NZ_Write), .en(1'b1), .Q(NZ_Write_2), .clk(clk));  // open: clr
  Register #(.width(1)) register_12 (.D(CV_Write), .en(1'b1), .Q(CV_Write_2), .clk(clk));  // open: clr
  Register #(.width(3)) register_13 (.D(Rd), .en(1'b1), .Q(Rd_2), .clk(clk));  // open: clr
  Register #(.width(32)) register_14 (.D(m_data), .en(1'b1), .Q(m_data_2), .clk(clk));  // open: clr
  Register #(.width(3)) register_15 (.D(Rm), .en(1'b1), .Q(Rm_2), .clk(clk));  // open: clr
  Register #(.width(3)) register_16 (.D(Rn), .en(1'b1), .Q(Rn_2), .clk(clk));  // open: clr
endmodule

// SR3
module SR_3 (
  input  clk,
  input  [31:0] alu_data,
  input  [31:0] m_data,
  input  V,
  input  C,
  input  Z,
  input  N,
  input  mem_write,
  input  mem_mux,
  input  [2:0] Rd,
  input  WB_write,
  output [31:0] alu_data_2,
  output [31:0] m_data_2,
  output V_2,
  output C_2,
  output Z_2,
  output N_2,
  output mem_write_2,
  output mem_mux_2,
  output [2:0] Rd_2,
  output WB_write_2
);

  Register #(.width(32)) register_1 (.D(alu_data), .en(1'b1), .Q(alu_data_2), .clk(clk));  // open: clr
  Register #(.width(32)) register_2 (.D(m_data), .en(1'b1), .Q(m_data_2), .clk(clk));  // open: clr
  Register #(.width(1)) register_3 (.D(V), .en(1'b1), .Q(V_2), .clk(clk));  // open: clr
  Register #(.width(1)) register_4 (.D(C), .en(1'b1), .Q(C_2), .clk(clk));  // open: clr
  Register #(.width(1)) register_5 (.D(Z), .en(1'b1), .Q(Z_2), .clk(clk));  // open: clr
  Register #(.width(1)) register_6 (.D(N), .en(1'b1), .Q(N_2), .clk(clk));  // open: clr
  Register #(.width(1)) register_7 (.D(mem_write), .en(1'b1), .Q(mem_write_2), .clk(clk));  // open: clr
  Register #(.width(1)) register_8 (.D(mem_mux), .en(1'b1), .Q(mem_mux_2), .clk(clk));  // open: clr
  Register #(.width(3)) register_9 (.D(Rd), .en(1'b1), .Q(Rd_2), .clk(clk));  // open: clr
  Register #(.width(1)) register_10 (.D(WB_write), .en(1'b1), .Q(WB_write_2), .clk(clk));  // open: clr
endmodule

module load_use_hazard (
  input  WB_write_dest,
  input  [2:0] wb_rd,
  input  [2:0] ex_rm,
  input  [2:0] ex_rn,
  output S1_mux,
  output S2_mux
);

  wire [2:0] and_1_out, and_2_out, bit_extender_1_out, xnor_1_out, xnor_2_out;

  assign bit_extender_1_out = {{2{1'b1}}, WB_write_dest};  // Bit_Extender bit_extender_1
  assign xnor_1_out = ~(wb_rd ^ ex_rm);  // XNOR_Gate xnor_1, 3 bits wide
  assign xnor_2_out = ~(wb_rd ^ ex_rn);  // XNOR_Gate xnor_2, 3 bits wide
  assign and_1_out = bit_extender_1_out & xnor_1_out;  // AND_Gate and_1, 3 bits wide
  assign and_2_out = bit_extender_1_out & xnor_2_out;  // AND_Gate and_2, 3 bits wide
  and and_3 (S1_mux, and_1_out[0], and_1_out[1], and_1_out[2]);
  and and_4 (S2_mux, and_2_out[0], and_2_out[1], and_2_out[2]);
endmodule
