// Logisim project lab4.circ as structural Verilog: 8 circuits, main circuit PipelinedARM
module implementation (
  input  CLK,
  output [31:0] IF_PC,
  output [15:0] IF_Instruction,
  output EX_N,
  output EX_Z,
  output EX_C,
  output EX_V,
  output WB_Write_Desination,
  output [2:0] WB_D_address,
  output [31:0] WB_D_data,
  output WB_Memory_write,
  output [6:0] WB_M_address,
  output [31:0] WB_M_data_in
);

  wire alu_1_p3, alu_1_p4, alu_1_p6, alu_1_p7, BFlush, CondBFlush, control_1_condb, control_1_cv_write,
       control_1_destinationwrite, control_1_mem_mux, control_1_memwrite, control_1_nz_write, De_B, Ex_BCond,
       hazard_control_1_s1_mux, hazard_control_1_s2_mux, not_1_out, not_2_out, or_1_out, sr2_1_cv_write_2,
       sr2_1_destinationwrite_2, sr2_1_mem_mux_2, sr2_1_memwrite_2, sr2_1_nz_write_2, sr3_1_mem_mux_2, stall;
  wire [1:0] control_1_alu_mux, control_1_rf_mux;
  wire [2:0] multiplexer_2_out, sr2_1_rd_2, sr2_1_rm_2, sr2_1_rn_2;
  wire [3:0] control_1_alu_op, Ex_Cond, sr2_1_alu_op_2;
  wire [7:0] Ex_imm11;
  wire [10:0] De_imm11, multiplexer_6_out;
  wire [15:11] INSTR;
  wire [15:12] sr2_1_instruction_2;
  wire [31:0] adder_1_out, alu_1_p8, bit_extender_1_out, bit_extender_2_out, De_PC, Ex_PC, multiplexer_1_out,
       multiplexer_3_out, multiplexer_4_out, multiplexer_5_out, multiplexer_7_out, NextPC, ram_2_data,
       register_file_1_p7, register_file_1_p8, sr2_1_m_data_2, sr2_1_s1_2, sr2_1_s2_2, sr3_1_alu_data_2,
       Wb_PC;

  Adder #(.width(32)) adder_1 (.a(IF_PC), .b(32'h2), .out(adder_1_out));  // open: cin, cout
  Multiplexer #(.width(32), .enable("false")) multiplexer_1 (
    .in0(adder_1_out), .in1(NextPC), .out(multiplexer_1_out), .sel(or_1_out));
  or or_1 (or_1_out, BFlush, CondBFlush);
  Register #(.width(32)) register_1 (.D(multiplexer_1_out), .en(not_1_out), .Q(IF_PC), .clk(CLK));  // open: clr
  not not_1 (not_1_out, stall);
  RAM #(.addrWidth(7), .dataWidth(16)) ram_1 (.addr(IF_PC[7:1]), .data(IF_Instruction));  // open: sel, clk, ld, clr
  SR1 sr1_1 (
    .Flush(or_1_out), .enable(stall), .clk(CLK), .Instruction(IF_Instruction), .PC(IF_PC),
    .Result({INSTR, De_imm11}), .PC_2(De_PC));
  control control_1 (
    .Op({INSTR, De_imm11[10:6]}), .B(De_B), .CondB(control_1_condb), .ALU_Op(control_1_alu_op),
    .RF_Mux(control_1_rf_mux), .ALU_Mux(control_1_alu_mux), .Mem_Mux(control_1_mem_mux),
    .MemWrite(control_1_memwrite), .DestinationWrite(control_1_destinationwrite),
    .NZ_Write(control_1_nz_write), .CV_Write(control_1_cv_write));
  Multiplexer #(.select(2), .width(3), .enable("false")) multiplexer_2 (
    .in0(De_imm11[5:3]), .in1(De_imm11[8:6]), .in2(De_imm11[2:0]), .in3(De_imm11[5:3]),
    .out(multiplexer_2_out), .sel(control_1_rf_mux));
  assign bit_extender_1_out = {{29{1'b0}}, multiplexer_2_out};  // Bit_Extender bit_extender_1
  assign bit_extender_2_out = {{25{1'b0}}, {De_imm11[10:6], 2'b00}};  // Bit_Extender bit_extender_2
  // Register_File register_file_1: pin names not known; wires that end beside it: De_imm11[5:3], multiplexer_2_out, WB_D_address, WB_D_data, WB_Write_Desination, CLK, register_file_1_p7, register_file_1_p8
  Multiplexer #(.select(2), .width(32), .enable("false")) multiplexer_3 (
    .in0(register_file_1_p8), .in1(bit_extender_2_out), .in2(bit_extender_1_out), .out(multiplexer_3_out),
    .sel(control_1_alu_mux));  // open: in3
  SR2 sr2_1 (
    .enable(stall), .clk(CLK), .S1(register_file_1_p7), .S2(multiplexer_3_out), .B(De_B),
    .CondB(control_1_condb), .ALU_Op(control_1_alu_op), .RF_Mux(control_1_rf_mux),
    .ALU_Mux(control_1_alu_mux), .Mem_Mux(control_1_mem_mux), .MemWrite(control_1_memwrite),
    .DestinationWrite(control_1_destinationwrite), .NZ_Write(control_1_nz_write),
    .CV_Write(control_1_cv_write), .Rd(De_imm11[2:0]), .m_data(register_file_1_p8), .Rm(multiplexer_2_out),
    .Rn(De_imm11[5:3]), .Instruction({INSTR, De_imm11}), .PC(De_PC), .Flush(CondBFlush), .S1_2(sr2_1_s1_2),
    .S2_2(sr2_1_s2_2), .CondB_2(Ex_BCond), .ALU_Op_2(sr2_1_alu_op_2), .Mem_Mux_2(sr2_1_mem_mux_2),
    .MemWrite_2(sr2_1_memwrite_2), .DestinationWrite_2(sr2_1_destinationwrite_2),
    .NZ_Write_2(sr2_1_nz_write_2), .CV_Write_2(sr2_1_cv_write_2), .Rd_2(sr2_1_rd_2),
    .m_data_2(sr2_1_m_data_2), .Rm_2(sr2_1_rm_2), .Rn_2(sr2_1_rn_2),
    .Instruction_2({sr2_1_instruction_2, Ex_Cond, Ex_imm11}), .PC_2(Ex_PC));  // open: B_2, RF_Mux_2, ALU_Mux_2
  Hazard_Control hazard_control_1 (
    .clk(CLK), .WB_write_dest(WB_Write_Desination), .wb_rd(WB_D_address), .ex_rm(sr2_1_rm_2),
    .ex_rn(sr2_1_rn_2), .Ex_Instruction({sr2_1_instruction_2, Ex_Cond, Ex_imm11}), .Ex_Rd(sr2_1_rd_2),
    .De_Rn(De_imm11[5:3]), .De_Rm(multiplexer_2_out), .Ex_Mem_mux(sr2_1_mem_mux_2), .Ex_PC(Ex_PC),
    .Wb_PC(Wb_PC), .De_Instruction({INSTR, De_imm11}), .S1_mux(hazard_control_1_s1_mux),
    .S2_mux(hazard_control_1_s2_mux), .Stall(stall));
  Multiplexer #(.width(32), .enable("false")) multiplexer_4 (
    .in0(sr2_1_s1_2), .in1(WB_D_data), .out(multiplexer_4_out), .sel(hazard_control_1_s1_mux));
  Multiplexer #(.width(32), .enable("false")) multiplexer_5 (
    .in0(sr2_1_s2_2), .in1(WB_D_data), .out(multiplexer_5_out), .sel(hazard_control_1_s2_mux));
  Multiplexer #(.width(11), .enable("false")) multiplexer_6 (
    .in0(De_imm11), .in1({Ex_Cond[2:0], Ex_imm11}), .out(multiplexer_6_out), .sel(Ex_BCond));
  // ALU alu_1: pin names not known; wires that end beside it: multiplexer_4_out, multiplexer_5_out, alu_1_p3, alu_1_p4, sr2_1_alu_op_2, alu_1_p6, alu_1_p7, alu_1_p8
  D_Flip_Flop d_ff_1 (.clk(CLK), .D(alu_1_p7), .Q(EX_V), .en(sr2_1_cv_write_2));  // open: Qn, preset, reset
  D_Flip_Flop d_ff_2 (.clk(CLK), .D(alu_1_p6), .Q(EX_C), .en(sr2_1_cv_write_2));  // open: Qn, preset, reset
  D_Flip_Flop d_ff_3 (.clk(CLK), .D(alu_1_p4), .Q(EX_Z), .en(sr2_1_nz_write_2));  // open: Qn, preset, reset
  D_Flip_Flop d_ff_4 (.clk(CLK), .D(alu_1_p3), .Q(EX_N), .en(sr2_1_nz_write_2));  // open: Qn, preset, reset
  Multiplexer #(.width(32), .enable("false")) multiplexer_7 (
    .in0(De_PC), .in1(Ex_PC), .out(multiplexer_7_out), .sel(Ex_BCond));
  Next_PC next_pc_1 (
    .PCplus2(multiplexer_7_out), .imm11(multiplexer_6_out), .B(De_B), .Bcond(Ex_BCond), .N(EX_N), .Z(EX_Z),
    .C(EX_C), .V(EX_V), .Cond(Ex_Cond), .BFlush(BFlush), .CondBFlush(CondBFlush), .NextPC(NextPC));
  SR3 sr3_1 (
    .enable(stall), .clk(CLK), .alu_data(alu_1_p8), .m_data(sr2_1_m_data_2), .V(EX_V), .C(EX_C), .Z(EX_Z),
    .N(EX_N), .mem_write(sr2_1_memwrite_2), .mem_mux(sr2_1_mem_mux_2), .Rd(sr2_1_rd_2),
    .WB_write(sr2_1_destinationwrite_2), .PC(Ex_PC),
    .alu_data_2({sr3_1_alu_data_2[31:9], WB_M_address, sr3_1_alu_data_2[1:0]}), .m_data_2(WB_M_data_in),
    .mem_write_2(WB_Memory_write), .mem_mux_2(sr3_1_mem_mux_2), .Rd_2(WB_D_address),
    .WB_write_2(WB_Write_Desination), .PC_2(Wb_PC));  // open: V_2, C_2, Z_2, N_2
  not not_2 (not_2_out, WB_Memory_write);
  RAM #(.addrWidth(7), .dataWidth(32), .bus("separate")) ram_2 (
    .addr(WB_M_address), .din(WB_M_data_in), .data(ram_2_data), .str(WB_Memory_write), .clk(CLK),
    .ld(not_2_out));  // open: sel, clr
  Multiplexer #(.width(32), .enable("false")) multiplexer_8 (
    .in0({sr3_1_alu_data_2[31:9], WB_M_address, sr3_1_alu_data_2[1:0]}), .in1(ram_2_data), .out(WB_D_data),
    .sel(sr3_1_mem_mux_2));

  // Other names for the same wires on the sheet: INSTR[10:0] = De_imm11; Ex_imm11[10:8] = Ex_Cond[2:0];
  //   WB_m_addr[6:0] = WB_M_address; WB_d_addr[2:0] = WB_D_address; WB_dest = WB_Write_Desination;
  //   WB_m_data[31:0] = WB_M_data_in; WB_mem_write = WB_Memory_write
endmodule

module PipelinedARM (
  input  CLK,
  output [31:0] IF_PC,
  output [15:0] IF_Instruction,
  output EX_N,
  output EX_Z,
  output EX_C,
  output EX_V,
  output WB_Write_Desination,
  output [2:0] WB_D_address,
  output [31:0] WB_D_data,
  output WB_Memory_write,
  output [6:0] WB_M_address,
  output [31:0] WB_M_data_in
);

  implementation implementation_1 (
    .CLK(CLK), .IF_PC(IF_PC), .IF_Instruction(IF_Instruction), .EX_N(EX_N), .EX_Z(EX_Z), .EX_C(EX_C),
    .EX_V(EX_V), .WB_Write_Desination(WB_Write_Desination), .WB_D_address(WB_D_address),
    .WB_D_data(WB_D_data), .WB_Memory_write(WB_Memory_write), .WB_M_address(WB_M_address),
    .WB_M_data_in(WB_M_data_in));

  // Notes on the sheet:
  //   Tim Whitaker
  //   Jay DiFuria
endmodule

module SR1 (
  input  Flush,
  input  enable,
  input  clk,
  input  [15:0] Instruction,
  input  [31:0] PC,
  output [15:0] Result,
  output [31:0] PC_2
);

  wire d_ff_1_q, not_1_out;

  not not_1 (not_1_out, enable);
  D_Flip_Flop d_ff_1 (.clk(clk), .D(Flush), .Q(d_ff_1_q));  // open: Qn, preset, en, reset
  Register #(.width(16)) register_1 (.D(Instruction), .en(not_1_out), .Q(Result), .clk(clk), .clr(d_ff_1_q));
  Register #(.width(32)) register_2 (.D(PC), .en(not_1_out), .Q(PC_2), .clk(clk), .clr(d_ff_1_q));
endmodule

module SR2 (
  input  enable,
  input  clk,
  input  [31:0] S1,
  input  [31:0] S2,
  input  B,
  input  CondB,
  input  [3:0] ALU_Op,
  input  [1:0] RF_Mux,
  input  [1:0] ALU_Mux,
  input  Mem_Mux,
  input  MemWrite,
  input  DestinationWrite,
  input  NZ_Write,
  input  CV_Write,
  input  [2:0] Rd,
  input  [31:0] m_data,
  input  [2:0] Rm,
  input  [2:0] Rn,
  input  [15:0] Instruction,
  input  [31:0] PC,
  input  Flush,
  output [31:0] S1_2,
  output [31:0] S2_2,
  output B_2,
  output CondB_2,
  output [3:0] ALU_Op_2,
  output [1:0] RF_Mux_2,
  output [1:0] ALU_Mux_2,
  output Mem_Mux_2,
  output MemWrite_2,
  output DestinationWrite_2,
  output NZ_Write_2,
  output CV_Write_2,
  output [2:0] Rd_2,
  output [31:0] m_data_2,
  output [2:0] Rm_2,
  output [2:0] Rn_2,
  output [15:0] Instruction_2,
  output [31:0] PC_2
);

  wire d_ff_1_q, not_1_out;

  not not_1 (not_1_out, enable);
  D_Flip_Flop d_ff_1 (.clk(clk), .D(Flush), .Q(d_ff_1_q));  // open: Qn, preset, en, reset
  Register #(.width(32)) register_1 (.D(S1), .en(not_1_out), .Q(S1_2), .clk(clk), .clr(d_ff_1_q));
  Register #(.width(32)) register_2 (.D(S2), .en(not_1_out), .Q(S2_2), .clk(clk), .clr(d_ff_1_q));
  Register #(.width(1)) register_3 (.D(B), .en(not_1_out), .Q(B_2), .clk(clk), .clr(d_ff_1_q));
  Register #(.width(1)) register_4 (.D(CondB), .en(not_1_out), .Q(CondB_2), .clk(clk), .clr(d_ff_1_q));
  Register #(.width(4)) register_5 (.D(ALU_Op), .en(not_1_out), .Q(ALU_Op_2), .clk(clk), .clr(d_ff_1_q));
  Register #(.width(2)) register_6 (.D(RF_Mux), .en(not_1_out), .Q(RF_Mux_2), .clk(clk), .clr(d_ff_1_q));
  Register #(.width(2)) register_7 (.D(ALU_Mux), .en(not_1_out), .Q(ALU_Mux_2), .clk(clk), .clr(d_ff_1_q));
  Register #(.width(1)) register_8 (.D(Mem_Mux), .en(not_1_out), .Q(Mem_Mux_2), .clk(clk), .clr(d_ff_1_q));
  Register #(.width(1)) register_9 (.D(MemWrite), .en(not_1_out), .Q(MemWrite_2), .clk(clk), .clr(d_ff_1_q));
  Register #(.width(1)) register_10 (
    .D(DestinationWrite), .en(not_1_out), .Q(DestinationWrite_2), .clk(clk), .clr(d_ff_1_q));
  Register #(.width(1)) register_11 (.D(NZ_Write), .en(not_1_out), .Q(NZ_Write_2), .clk(clk), .clr(d_ff_1_q));
  Register #(.width(1)) register_12 (.D(CV_Write), .en(not_1_out), .Q(CV_Write_2), .clk(clk), .clr(d_ff_1_q));
  Register #(.width(3)) register_13 (.D(Rd), .en(not_1_out), .Q(Rd_2), .clk(clk), .clr(d_ff_1_q));
  Register #(.width(32)) register_14 (.D(m_data), .en(not_1_out), .Q(m_data_2), .clk(clk), .clr(d_ff_1_q));
  Register #(.width(3)) register_15 (.D(Rm), .en(not_1_out), .Q(Rm_2), .clk(clk), .clr(d_ff_1_q));
  Register #(.width(3)) register_16 (.D(Rn), .en(not_1_out), .Q(Rn_2), .clk(clk), .clr(d_ff_1_q));
  Register #(.width(16)) register_17 (.D(Instruction), .en(not_1_out), .Q(Instruction_2), .clk(clk), .clr(d_ff_1_q));
  Register #(.width(32)) register_18 (.D(PC), .en(not_1_out), .Q(PC_2), .clk(clk), .clr(d_ff_1_q));
endmodule

module SR3 (
  input  enable,
  input  clk,
  input  [31:0] alu_data,
  input  [31:0] m_data,
  input  V,
  input  C,
  input  Z,
  input  N,
  input  mem_write,
  input  mem_mux,
  input  [2:0] Rd,
  input  WB_write,
  input  [31:0] PC,
  output [31:0] alu_data_2,
  output [31:0] m_data_2,
  output V_2,
  output C_2,
  output Z_2,
  output N_2,
  output mem_write_2,
  output mem_mux_2,
  output [2:0] Rd_2,
  output WB_write_2,
  output [31:0] PC_2
);

  wire d_ff_1_q, multiplexer_1_out, multiplexer_2_out;

  D_Flip_Flop d_ff_1 (.clk(clk), .D(enable), .Q(d_ff_1_q));  // open: Qn, preset, en, reset
  Multiplexer #(.enable("false")) multiplexer_1 (.in0(mem_write), .in1(1'b0), .out(multiplexer_1_out), .sel(d_ff_1_q));
  Multiplexer #(.enable("false")) multiplexer_2 (.in0(WB_write), .in1(1'b0), .out(multiplexer_2_out), .sel(d_ff_1_q));
  Register #(.width(32)) register_1 (.D(alu_data), .en(1'b1), .Q(alu_data_2), .clk(clk));  // open: clr
  Register #(.width(32)) register_2 (.D(m_data), .en(1'b1), .Q(m_data_2), .clk(clk));  // open: clr
  Register #(.width(1)) register_3 (.D(V), .en(1'b1), .Q(V_2), .clk(clk));  // open: clr
  Register #(.width(1)) register_4 (.D(C), .en(1'b1), .Q(C_2), .clk(clk));  // open: clr
  Register #(.width(1)) register_5 (.D(Z), .en(1'b1), .Q(Z_2), .clk(clk));  // open: clr
  Register #(.width(1)) register_6 (.D(N), .en(1'b1), .Q(N_2), .clk(clk));  // open: clr
  Register #(.width(1)) register_7 (.D(multiplexer_1_out), .en(1'b1), .Q(mem_write_2), .clk(clk));  // open: clr
  Register #(.width(1)) register_8 (.D(mem_mux), .en(1'b1), .Q(mem_mux_2), .clk(clk));  // open: clr
  Register #(.width(3)) register_9 (.D(Rd), .en(1'b1), .Q(Rd_2), .clk(clk));  // open: clr
  Register #(.width(1)) register_10 (.D(multiplexer_2_out), .en(1'b1), .Q(WB_write_2), .clk(clk));  // open: clr
  Register #(.width(32)) register_11 (.D(PC), .en(1'b1), .Q(PC_2), .clk(clk));  // open: clr
endmodule

module Hazard_Control (
  input  clk,
  input  WB_write_dest,
  input  [2:0] wb_rd,
  input  [2:0] ex_rm,
  input  [2:0] ex_rn,
  input  [15:0] Ex_Instruction,
  input  [2:0] Ex_Rd,
  input  [2:0] De_Rn,
  input  [2:0] De_Rm,
  input  Ex_Mem_mux,
  input  [31:0] Ex_PC,
  input  [31:0] Wb_PC,
  input  [15:0] De_Instruction,
  output S1_mux,
  output S2_mux,
  output Stall
);

  wire and_5_out, and_6_out, and_7_out, and_8_out, and_9_out, and_10_out, and_11_out, and_12_out, and_13_out,
       comparator_1_eq, comparator_2_eq, comparator_3_eq, comparator_4_eq, comparator_5_eq, comparator_6_eq,
       comparator_7_eq, comparator_8_eq, comparator_9_eq, comparator_10_eq, comparator_11_eq,
       comparator_12_eq, comparator_13_eq, comparator_14_eq, comparator_15_eq, comparator_16_eq, d_ff_1_q,
       d_ff_2_q, or_1_out, or_2_out, or_3_out, or_4_out, or_5_out, or_6_out;
  wire [2:0] and_1_out, and_2_out, and_3_out, and_4_out, bit_extender_1_out, bit_extender_2_out, xnor_1_out,
       xnor_2_out, xnor_3_out, xnor_4_out;

  assign bit_extender_1_out = {{2{1'b1}}, WB_write_dest};  // Bit_Extender bit_extender_1
  assign xnor_1_out = ~(wb_rd ^ ex_rn);  // XNOR_Gate xnor_1, 3 bits wide
  assign xnor_2_out = ~(wb_rd ^ ex_rm);  // XNOR_Gate xnor_2, 3 bits wide
  Comparator #(.width(6)) comparator_1 (
    .a(6'b010000), .b(Ex_Instruction[15:10]), .eq(comparator_1_eq));  // open: gt, lt
  Comparator #(.width(7)) comparator_2 (
    .a(Ex_Instruction[15:9]), .b(7'b0001100), .eq(comparator_2_eq));  // open: gt, lt
  Comparator #(.width(7)) comparator_3 (
    .a(Ex_Instruction[15:9]), .b(7'b0001110), .eq(comparator_3_eq));  // open: gt, lt
  Comparator #(.width(7)) comparator_4 (
    .a(Ex_Instruction[15:9]), .b(7'b0001101), .eq(comparator_4_eq));  // open: gt, lt
  Comparator #(.width(7)) comparator_5 (
    .a(Ex_Instruction[15:9]), .b(7'b0001111), .eq(comparator_5_eq));  // open: gt, lt
  Comparator #(.width(5)) comparator_6 (.a(Ex_Instruction[15:11]), .b(5'b01010), .eq(comparator_6_eq));  // open: gt, lt
  Comparator #(.width(5)) comparator_7 (.a(Ex_Instruction[15:11]), .b(5'b01100), .eq(comparator_7_eq));  // open: gt, lt
  Comparator #(.width(5)) comparator_8 (.a(Ex_Instruction[15:11]), .b(5'b01011), .eq(comparator_8_eq));  // open: gt, lt
  Comparator #(.width(5)) comparator_9 (.a(Ex_Instruction[15:11]), .b(5'b01101), .eq(comparator_9_eq));  // open: gt, lt
  Comparator #(.width(16)) comparator_10 (.a(Ex_Instruction), .b(16'hbf00), .eq(comparator_10_eq));  // open: gt, lt
  assign xnor_3_out = ~(Ex_Rd ^ De_Rn);  // XNOR_Gate xnor_3, 3 bits wide
  assign xnor_4_out = ~(Ex_Rd ^ De_Rm);  // XNOR_Gate xnor_4, 3 bits wide
  assign bit_extender_2_out = {{2{1'b1}}, Ex_Mem_mux};  // Bit_Extender bit_extender_2
  Comparator #(.width(32)) comparator_11 (.a(Ex_PC), .b(Wb_PC), .eq(comparator_11_eq));  // open: gt, lt
  Comparator #(.width(32)) comparator_12 (.a(Wb_PC), .b({32{1'b0}}), .eq(comparator_12_eq));  // open: gt, lt
  Comparator #(.width(7)) comparator_13 (
    .a(De_Instruction[15:9]), .b(7'b0001100), .eq(comparator_13_eq));  // open: gt, lt
  Comparator #(.width(7)) comparator_14 (
    .a(De_Instruction[15:9]), .b(7'b0001110), .eq(comparator_14_eq));  // open: gt, lt
  Comparator #(.width(7)) comparator_15 (
    .a(De_Instruction[15:9]), .b(7'b0001101), .eq(comparator_15_eq));  // open: gt, lt
  Comparator #(.width(7)) comparator_16 (
    .a(De_Instruction[15:9]), .b(7'b0001111), .eq(comparator_16_eq));  // open: gt, lt
  assign and_1_out = bit_extender_1_out & xnor_1_out;  // AND_Gate and_1, 3 bits wide
  assign and_2_out = bit_extender_1_out & xnor_2_out;  // AND_Gate and_2, 3 bits wide
  assign and_3_out = xnor_3_out & bit_extender_2_out;  // AND_Gate and_3, 3 bits wide
  assign and_4_out = xnor_4_out & bit_extender_2_out;  // AND_Gate and_4, 3 bits wide
  and and_5 (and_5_out, comparator_11_eq, ~comparator_12_eq);  // AND_Gate
  and and_6 (and_6_out, and_3_out[0], and_3_out[1], and_3_out[2]);
  and and_7 (and_7_out, and_4_out[0], and_4_out[1], and_4_out[2]);
  or or_1 (or_1_out, comparator_14_eq, comparator_16_eq);
  and and_8 (and_8_out, and_1_out[0], and_1_out[1], and_1_out[2]);
  and and_9 (and_9_out, and_2_out[0], and_2_out[1], and_2_out[2]);
  or or_2 (or_2_out, comparator_3_eq, comparator_5_eq);
  or or_3 (or_3_out, comparator_8_eq, comparator_9_eq);
  and and_10 (and_10_out, and_9_out, ~or_2_out);  // AND_Gate
  and and_11 (and_11_out, or_3_out, and_6_out);
  and and_12 (and_12_out, or_3_out, and_7_out);
  and and_13 (and_13_out, and_12_out, ~or_1_out);  // AND_Gate
  D_Flip_Flop d_ff_1 (.clk(clk), .D(and_11_out), .Q(d_ff_1_q), .en(1'b1));  // open: Qn, preset, reset
  D_Flip_Flop d_ff_2 (.clk(clk), .D(and_13_out), .Q(d_ff_2_q), .en(1'b1));  // open: Qn, preset, reset
  or or_4 (or_4_out, and_8_out, d_ff_1_q);
  or or_5 (or_5_out, and_10_out, d_ff_2_q);
  or or_6 (or_6_out, and_11_out, and_13_out);
  and and_14 (S1_mux, or_4_out, ~and_5_out);  // AND_Gate
  and and_15 (S2_mux, or_5_out, ~and_5_out);  // AND_Gate
  and and_16 (Stall, or_6_out, ~and_5_out);  // AND_Gate

  // Notes on the sheet:
  //   add reg
  //   add imm
  //   sub reg
  //   sub imm
  //   register manip
  //   add reg
  //   add imm
  //   sub reg
  //   sub imm
  //   store reg
  //   store imm
  //   load reg
  //   load imm
  //   nop
endmodule

module control (
  input  [9:0] Op,
  output B,
  output CondB,
  output [3:0] ALU_Op,
  output [1:0] RF_Mux,
  output [1:0] ALU_Mux,
  output Mem_Mux,
  output MemWrite,
  output DestinationWrite,
  output NZ_Write,
  output CV_Write
);

  wire and_1_out, and_4_out, comparator_1_eq, decoder_1_out4, decoder_1_out11;
  wire [3:0] multiplexer_1_out, multiplexer_2_out;

  Decoder #(.select(4), .enable("false")) decoder_1 (
    .out1(CV_Write), .out4(decoder_1_out4), .out6(ALU_Mux[0]), .out11(decoder_1_out11), .out13(CondB),
    .out14(B), .sel(Op[9:6]));  // open: out0, out2, out3, out5, out7, out8, out9, out10, out12, out15
  Multiplexer #(.width(4), .enable("false")) multiplexer_1 (
    .in0(4'b1011), .in1(4'b1010), .out(multiplexer_1_out), .sel(Op[3]));
  Comparator #(.width(4)) comparator_1 (.a(Op[3:0]), .b(4'b1111), .eq(comparator_1_eq));  // open: gt, lt
  Multiplexer #(.width(4), .enable("false")) multiplexer_2 (
    .in0(multiplexer_1_out), .in1(4'b1011), .out(multiplexer_2_out), .sel(ALU_Mux[0]));
  Multiplexer #(.width(4), .enable("false")) multiplexer_3 (
    .in0(multiplexer_2_out), .in1(Op[3:0]), .out(ALU_Op), .sel(decoder_1_out4));
  and and_1 (and_1_out, comparator_1_eq, decoder_1_out4);
  and and_2 (ALU_Mux[1], CV_Write, Op[4]);
  and and_3 (MemWrite, ALU_Mux[0], ~Op[5]);  // AND_Gate
  and and_4 (and_4_out, Op[5], ALU_Mux[0]);
  or or_1 (DestinationWrite, and_4_out, decoder_1_out4, CV_Write);
  or or_2 (NZ_Write, CV_Write, decoder_1_out4);
  or or_3 (RF_Mux[0], and_1_out, CV_Write);
  or or_4 (RF_Mux[1], ALU_Mux[0], decoder_1_out4);

  assign Mem_Mux = ALU_Mux[0];

  // Notes on the sheet:
  //   B
  //   B{cond}
  //   REGS
  //   NOP
  //   LDR/STR
  //   ADDS/SUBS
endmodule

module Next_PC (
  input  [31:0] PCplus2,
  input  [10:0] imm11,
  input  B,
  input  Bcond,
  input  N,
  input  Z,
  input  C,
  input  V,
  input  [3:0] Cond,
  output BFlush,
  output CondBFlush,
  output [31:0] NextPC
);

  wire multiplexer_3_out, not_1_out, not_2_out, not_3_out, not_4_out;
  wire [31:0] adder_1_out, adder_2_out, adder_3_out, adder_4_out, adder_5_out, bit_extender_1_out,
       bit_extender_2_out, multiplexer_1_out;

  Adder #(.width(32)) adder_1 (.a(32'h2), .b(PCplus2), .out(adder_1_out));  // open: cin, cout
  assign bit_extender_1_out = {{20{imm11[10]}}, {imm11, 1'b0}};  // Bit_Extender bit_extender_1
  Adder #(.width(32)) adder_2 (.a(adder_1_out), .b(bit_extender_1_out), .out(adder_2_out), .cin(1'b0));  // open: cout
  Adder #(.width(32)) adder_3 (.a(32'h2), .b(adder_2_out), .out(adder_3_out));  // open: cin, cout
  assign bit_extender_2_out = {{23{imm11[7]}}, {imm11[7:0], 1'b0}};  // Bit_Extender bit_extender_2
  Adder #(.width(32)) adder_4 (.a(32'h2), .b(adder_5_out), .out(adder_4_out));  // open: cin, cout
  Adder #(.width(32)) adder_5 (.a(adder_1_out), .b(bit_extender_2_out), .out(adder_5_out), .cin(1'b0));  // open: cout
  not not_1 (not_1_out, Z);
  not not_2 (not_2_out, C);
  not not_3 (not_3_out, N);
  not not_4 (not_4_out, V);
  Multiplexer #(.width(32), .enable("false")) multiplexer_1 (
    .in0(adder_1_out), .in1(adder_3_out), .out(multiplexer_1_out), .sel(B));
  Multiplexer #(.width(32), .enable("false")) multiplexer_2 (
    .in0(multiplexer_1_out), .in1(adder_4_out), .out(NextPC), .sel(CondBFlush));
  and and_1 (CondBFlush, Bcond, multiplexer_3_out);
  Multiplexer #(.select(4), .enable("false")) multiplexer_3 (
    .in0(Z), .in1(not_1_out), .in2(C), .in3(not_2_out), .in4(N), .in5(not_3_out), .in6(V), .in7(not_4_out),
    .in8(1'b0), .in9(1'b0), .in10(1'b0), .in11(1'b0), .in12(1'b0), .in13(1'b0), .in14(1'b0), .in15(1'b0),
    .out(multiplexer_3_out), .sel(Cond));

  assign BFlush = B;
endmodule
