// Logisim project lab5.circ as structural Verilog: 3 circuits, main circuit Cache
module Cache (
  input  [31:0] Address,
  input  CLK,
  output Hit,
  output [15:0] Data
);

  wire and_1_out, cache_block_1_hit, cache_block_2_hit, cache_block_3_hit, cache_block_4_hit, not_1_out,
       or_1_out, slowmemory_1_ready;
  wire [15:0] cache_block_1_data_2, cache_block_2_data_2, cache_block_3_data_2, cache_block_4_data_2,
       multiplexer_1_out, multiplexer_2_out;
  wire [31:0] slowmemory_1_data;

  cache_block cache_block_1 (
    .addr(Address), .data(slowmemory_1_data), .ready(slowmemory_1_ready), .clk(CLK), .block_num(2'b00),
    .data_2(cache_block_1_data_2), .hit(cache_block_1_hit));
  cache_block cache_block_2 (
    .addr(Address), .data(slowmemory_1_data), .ready(slowmemory_1_ready), .clk(CLK), .block_num(2'b01),
    .data_2(cache_block_2_data_2), .hit(cache_block_2_hit));
  cache_block cache_block_3 (
    .addr(Address), .data(slowmemory_1_data), .ready(slowmemory_1_ready), .clk(CLK), .block_num(2'b10),
    .data_2(cache_block_3_data_2), .hit(cache_block_3_hit));
  cache_block cache_block_4 (
    .addr(Address), .data(slowmemory_1_data), .ready(slowmemory_1_ready), .clk(CLK), .block_num(2'b11),
    .data_2(cache_block_4_data_2), .hit(cache_block_4_hit));
  SlowMemory slowmemory_1 (
    .Addr(Address), .CLK(CLK), .Data(slowmemory_1_data), .Ready(slowmemory_1_ready));  // open: Clear
  Multiplexer #(.width(16), .enable("false")) multiplexer_1 (
    .in0(slowmemory_1_data[15:0]), .in1(slowmemory_1_data[31:16]), .out(multiplexer_1_out), .sel(Address[1]));
  or or_1 (or_1_out, cache_block_1_hit, cache_block_2_hit, cache_block_3_hit, cache_block_4_hit);
  Multiplexer #(.select(2), .width(16), .enable("false")) multiplexer_2 (
    .in0(cache_block_1_data_2), .in1(cache_block_2_data_2), .in2(cache_block_3_data_2),
    .in3(cache_block_4_data_2), .out(multiplexer_2_out), .sel(Address[3:2]));
  or or_2 (Hit, slowmemory_1_ready, or_1_out);
  and and_1 (and_1_out, slowmemory_1_ready, not_1_out);
  not not_1 (not_1_out, or_1_out);
  Multiplexer #(.width(16), .enable("false")) multiplexer_3 (
    .in0(multiplexer_2_out), .in1(multiplexer_1_out), .out(Data), .sel(and_1_out));

  // Other names for the same wires on the sheet: offset = Address[1]; index[1:0] = Address[3:2];
  //   tag[27:0] = Address[31:4]

  // Notes on the sheet:
  //   Tim Whitaker, Jay DiFuria
endmodule

module SlowMemory (
  input  [31:0] Addr,
  input  CLK,
  input  Clear,
  output [31:0] Data,
  output Ready
);

  wire comparator_1_eq, comparator_2_eq, comparator_3_eq;
  wire [31:0] ram_1_data, register_1_q, register_2_q, register_3_q;

  Register #(.width(32)) register_1 (.D(Addr), .en(1'b1), .Q(register_1_q), .clk(CLK), .clr(Clear));
  Register #(.width(32)) register_2 (.D(register_1_q), .en(1'b1), .Q(register_2_q), .clk(CLK), .clr(Clear));
  Register #(.width(32)) register_3 (.D(register_2_q), .en(1'b1), .Q(register_3_q), .clk(CLK), .clr(Clear));
  Comparator #(.width(32), .mode("unsigned")) comparator_1 (
    .a(register_3_q), .b(register_2_q), .eq(comparator_1_eq));  // open: gt, lt
  Comparator #(.width(32), .mode("unsigned")) comparator_2 (
    .a(register_2_q), .b(register_1_q), .eq(comparator_2_eq));  // open: gt, lt
  Comparator #(.width(32), .mode("unsigned")) comparator_3 (
    .a(register_1_q), .b(Addr), .eq(comparator_3_eq));  // open: gt, lt
  and and_1 (Ready, comparator_1_eq, comparator_2_eq, comparator_3_eq);
  RAM #(.addrWidth(7), .dataWidth(32), .bus("asynch")) ram_1 (
    .addr(register_3_q[8:2]), .data(ram_1_data), .sel(1'b1), .ld(1'b1), .clr(Clear));
  assign Data = Ready ? ram_1_data : 32'bz;  // Controlled_Buffer controlled_buffer_1
endmodule

module cache_block (
  input  [31:0] addr,
  input  [31:0] data,
  input  ready,
  input  clk,
  input  [1:0] block_num,
  output [15:0] data_2,
  output hit
);

  wire and_1_out, and_2_out, and_3_out, comparator_1_eq, comparator_2_eq, miss, register_3_q;
  wire [27:0] register_2_q;
  wire [31:0] register_1_q;

  Comparator #(.width(28)) comparator_1 (.a(register_2_q), .b(addr[31:4]), .eq(comparator_1_eq));  // open: gt, lt
  Comparator #(.width(2)) comparator_2 (.a(addr[3:2]), .b(block_num), .eq(comparator_2_eq));  // open: gt, lt
  and and_1 (and_1_out, comparator_2_eq, ready);
  and and_2 (and_2_out, miss, and_1_out);
  Register #(.width(32)) register_1 (.D(data), .en(and_1_out), .Q(register_1_q), .clk(clk));  // open: clr
  and and_3 (and_3_out, and_1_out, miss);
  Register #(.width(28)) register_2 (.D(addr[31:4]), .en(and_2_out), .Q(register_2_q), .clk(clk));  // open: clr
  Register #(.width(1)) register_3 (.D(1'b1), .en(and_3_out), .Q(register_3_q), .clk(clk));  // open: clr
  Multiplexer #(.width(16), .enable("false")) multiplexer_1 (
    .in0(register_1_q[15:0]), .in1(register_1_q[31:16]), .out(data_2), .sel(addr[1]));
  and and_4 (hit, comparator_1_eq, comparator_2_eq, register_3_q);
  not not_1 (miss, hit);

  // Notes on the sheet:
  //   tag
  //   data
  //   valid
endmodule
